// Logisim project circuito.circ as structural Verilog: 4 circuits, main circuit main
module main (
  input  [7:0] data
);

  wire banco_de_dados_1_data_ok, banco_de_dados_1_k___textsize, banco_de_dados_1_pronto,
       bloco_de_controle_1_a_plus, bloco_de_controle_1_done, bloco_de_controle_1_en_i,
       bloco_de_controle_1_en_j, bloco_de_controle_1_en_k, bloco_de_controle_1_en_t, bloco_de_controle_1_ld,
       bloco_de_controle_1_out_15, bloco_de_controle_1_rst_bd, bloco_de_controle_1_sel,
       bloco_de_controle_1_vetor, clock_1_out, data_av_out, not_1_out, rst_out;
  wire [1:0] bloco_de_controle_1_b_plus, bloco_de_controle_1_dado, bloco_de_controle_1_indice;
  wire [7:0] banco_de_dados_1_a, banco_de_dados_1_data_out, ram_1_data, register_1_q;

  Button data_av (.out(data_av_out));
  Button rst (.out(rst_out));
  Clock clock_1 (.out(clock_1_out));
  Bloco_de_controle bloco_de_controle_1 (
    .data_ok(banco_de_dados_1_data_ok), .clk(clock_1_out), .en_k(bloco_de_controle_1_en_k),
    .vetor(bloco_de_controle_1_vetor), .en_i(bloco_de_controle_1_en_i), .out_15(bloco_de_controle_1_out_15),
    .Dado(bloco_de_controle_1_dado), .sel(bloco_de_controle_1_sel), .ld(bloco_de_controle_1_ld),
    .en_j(bloco_de_controle_1_en_j), .B_plus(bloco_de_controle_1_b_plus),
    .A_plus(bloco_de_controle_1_a_plus), .en_t(bloco_de_controle_1_en_t),
    .k___textSize(banco_de_dados_1_k___textsize), .pronto(banco_de_dados_1_pronto),
    .Done(bloco_de_controle_1_done), .indice(bloco_de_controle_1_indice),
    .rst_bd(bloco_de_controle_1_rst_bd), .rst(rst_out));
  Banco_de_Dados banco_de_dados_1 (
    .rst_bd(bloco_de_controle_1_rst_bd), .en_j(bloco_de_controle_1_en_j), .en_k(bloco_de_controle_1_en_k),
    .en_i(bloco_de_controle_1_en_i), .in_2(bloco_de_controle_1_out_15),
    .k___textSize(banco_de_dados_1_k___textsize), .en_t(bloco_de_controle_1_en_t),
    .Dado(bloco_de_controle_1_dado), .A_plus(bloco_de_controle_1_a_plus),
    .B_plus(bloco_de_controle_1_b_plus), .vetor(bloco_de_controle_1_vetor),
    .\índice (bloco_de_controle_1_indice), .pronto(banco_de_dados_1_pronto), .A(banco_de_dados_1_a),
    .data_in(register_1_q), .clk(clock_1_out), .data_out(banco_de_dados_1_data_out), .data(data),
    .data_av(data_av_out), .data_ok(banco_de_dados_1_data_ok), .rst(rst_out));
  LED led_1 (.in(bloco_de_controle_1_done));
  RAM ram_1 (
    .addr(banco_de_dados_1_a), .data(ram_1_data), .sel(bloco_de_controle_1_sel), .clk(clock_1_out),
    .ld(bloco_de_controle_1_ld));  // open: clr
  assign ram_1_data = not_1_out ? banco_de_dados_1_data_out : 8'bz;  // Controlled_Buffer controlled_buffer_1
  not not_1 (not_1_out, bloco_de_controle_1_ld);
  Register register_1 (.D(ram_1_data), .en(bloco_de_controle_1_sel), .Q(register_1_q), .clk(clock_1_out));  // open: clr
endmodule

module Banco_de_Dados (
  input  rst_bd,
  input  in_2,
  input  [7:0] data,
  input  vetor,
  input  en_i,
  input  rst,
  input  en_j,
  input  [1:0] \índice ,
  input  [1:0] Dado,
  input  en_k,
  input  en_t,
  input  data_av,
  input  A_plus,
  input  [1:0] B_plus,
  input  [7:0] data_in,
  input  clk,
  output pronto,
  output k___textSize,
  output data_ok,
  output [7:0] A,
  output [7:0] data_out
);

  wire adder_1_cout, and_1_out, and_2_out, and_4_out, and_5_out, and_6_out, d_ff_1_q, decoder_1_out0,
       decoder_1_out1, decoder_1_out2, decoder_1_out3, FF0_q, FF1_q, not_1_out, not_2_out, not_3_out,
       not_4_out, or_1_out;
  wire [1:0] adder_1_out, av_atual_q;
  wire [7:0] adder_3_out, i_q, j_q, k_q, KeyStream_q, multiplexer_1_out, multiplexer_2_out,
       multiplexer_3_out, multiplexer_5_out, multiplexer_6_out, multiplexer_7_out, multiplexer_8_out,
       multiplexer_9_out, register_1_q, state_q, stateSize_q, subtractor_1_out, t_q, textSize_q;

  or or_1 (or_1_out, FF1_q, FF0_q);
  not not_1 (not_1_out, FF1_q);
  not not_2 (not_2_out, FF0_q);
  and and_1 (and_1_out, or_1_out, data_av);
  and and_2 (and_2_out, not_1_out, not_2_out, data_av);
  D_Flip_Flop FF1 (.clk(clk), .D(and_1_out), .Q(FF1_q));  // open: Qn, preset, en, reset
  D_Flip_Flop FF0 (.clk(clk), .D(and_2_out), .Q(FF0_q));  // open: Qn, preset, en, reset
  and and_3 (data_ok, adder_1_cout, and_5_out);
  not not_3 (not_3_out, FF1_q);
  and and_4 (and_4_out, not_3_out, FF0_q);
  Adder #(.width(2)) adder_1 (.a(av_atual_q), .b(2'b01), .out(adder_1_out), .cout(adder_1_cout));  // open: cin
  and and_5 (and_5_out, and_4_out, rst_bd);
  Decoder #(.select(2), .disabled(0)) decoder_1 (
    .out0(decoder_1_out0), .out1(decoder_1_out1), .out2(decoder_1_out2), .out3(decoder_1_out3),
    .sel(av_atual_q), .en(and_5_out));
  Register #(.width(2)) av_atual (.D(adder_1_out), .en(and_5_out), .Q(av_atual_q), .clk(clk), .clr(rst));
  Register textSize (.D(data), .en(decoder_1_out2), .Q(textSize_q), .clk(clk));  // open: clr
  Register stateSize (.D(data), .en(decoder_1_out1), .Q(stateSize_q), .clk(clk));  // open: clr
  Register state (.D(data), .en(decoder_1_out0), .Q(state_q), .clk(clk));  // open: clr
  Register KeyStream (.D(data), .en(decoder_1_out3), .Q(KeyStream_q), .clk(clk));  // open: clr
  Multiplexer #(.width(8)) multiplexer_1 (
    .in0(textSize_q), .in1(stateSize_q), .out(multiplexer_1_out), .sel(in_2));  // open: en
  Multiplexer #(.width(8)) multiplexer_2 (
    .in0(multiplexer_5_out), .in1(adder_3_out), .out(multiplexer_2_out), .sel(k___textSize));  // open: en
  Register register_1 (.D(multiplexer_2_out), .en(and_6_out), .Q(register_1_q), .clk(clk), .clr(rst_bd));
  and and_6 (and_6_out, in_2, not_4_out);
  Multiplexer #(.width(8)) multiplexer_3 (
    .in0(k_q), .in1(register_1_q), .out(multiplexer_3_out), .sel(in_2));  // open: en
  Multiplexer #(.select(2), .width(8)) multiplexer_4 (
    .in0(adder_3_out), .in1(t_q), .in2(data_in), .in3(multiplexer_5_out), .out(data_out), .sel(Dado));  // open: en
  not not_4 (not_4_out, pronto);
  Register i (.D(data_out), .en(en_i), .Q(i_q), .clk(clk), .clr(rst_bd));
  Register j (.D(data_out), .en(en_j), .Q(j_q), .clk(clk), .clr(rst_bd));
  Register k (.D(data_out), .en(en_k), .Q(k_q), .clk(clk), .clr(rst_bd));
  Register t (.D(data_out), .en(en_t), .Q(t_q), .clk(clk), .clr(rst_bd));
  Multiplexer #(.width(8)) multiplexer_5 (
    .in0(subtractor_1_out), .in1(register_1_q), .out(multiplexer_5_out), .sel(k___textSize));  // open: en
  Subtractor subtractor_1 (
    .a(multiplexer_3_out), .b(multiplexer_1_out), .out(subtractor_1_out), .bout(k___textSize));  // open: bin
  Multiplexer #(.width(8)) multiplexer_6 (
    .in0(state_q), .in1(KeyStream_q), .out(multiplexer_6_out), .sel(vetor));  // open: en
  D_Flip_Flop d_ff_1 (.clk(clk), .D(in_2), .Q(d_ff_1_q), .reset(rst_bd));  // open: Qn, preset, en
  Multiplexer #(.select(2), .width(8)) multiplexer_7 (
    .in0(i_q), .in1(j_q), .in2(k_q), .in3(t_q), .out(multiplexer_7_out), .sel(\índice ));  // open: en
  Multiplexer #(.width(8)) multiplexer_8 (
    .in0(8'h1), .in1(data_in), .out(multiplexer_8_out), .sel(A_plus));  // open: en
  Multiplexer #(.select(2), .width(8)) multiplexer_9 (
    .in0(i_q), .in1(j_q), .in2(t_q), .in3(k_q), .out(multiplexer_9_out), .sel(B_plus));  // open: en
  Adder adder_2 (.a(multiplexer_6_out), .b(multiplexer_7_out), .out(A));  // open: cin, cout
  Adder adder_3 (.a(multiplexer_8_out), .b(multiplexer_9_out), .out(adder_3_out));  // open: cin, cout
  and and_7 (pronto, k___textSize, d_ff_1_q);
endmodule

module Bloco_de_controle (
  input  k___textSize,
  input  pronto,
  input  clk,
  input  data_ok,
  input  rst,
  output Done,
  output en_k,
  output en_j,
  output en_i,
  output en_t,
  output vetor,
  output [1:0] Dado,
  output sel,
  output ld,
  output out_15,
  output [1:0] B_plus,
  output A_plus,
  output [1:0] indice,
  output rst_bd
);

  wire and_1_out, and_2_out, and_3_out, and_4_out, and_5_out, and_6_out, and_7_out, and_8_out, and_9_out,
       and_10_out, and_11_out, and_12_out, and_13_out, and_14_out, and_15_out, and_16_out, and_17_out,
       and_19_out, and_20_out, and_21_out, and_22_out, and_23_out, and_24_out, and_25_out, and_26_out,
       and_27_out, and_28_out, and_29_out, and_30_out, and_31_out, and_32_out, and_33_out, and_34_out,
       and_40_out, and_41_out, and_42_out, and_43_out, and_44_out, and_45_out, and_46_out, and_47_out,
       and_48_out, nor_1_out, not_1_out, not_2_out, not_3_out, not_4_out, not_5_out, not_6_out, not_7_out,
       not_8_out, not_9_out, not_10_out, not_11_out, not_12_out, not_13_out, not_14_out, not_15_out,
       not_16_out, not_17_out, not_18_out, not_19_out, not_20_out, not_21_out, not_22_out, not_23_out,
       not_24_out, not_25_out, not_26_out, not_27_out, not_28_out, not_29_out, not_30_out, not_31_out,
       not_32_out, not_33_out, not_34_out, not_35_out, not_36_out, not_37_out, not_38_out, not_39_out,
       not_40_out, not_41_out, not_42_out, not_43_out, not_44_out, not_45_out, not_46_out, not_47_out,
       not_48_out, not_49_out, not_50_out, not_51_out, not_52_out, not_53_out, not_54_out, not_55_out,
       not_56_out, not_57_out, not_58_out, or_1_out, or_2_out, or_3_out, or_4_out, Q0_q, Q1_q, Q2_q, Q3_q;

  not not_1 (not_1_out, Q1_q);
  not not_2 (not_2_out, Q0_q);
  not not_3 (not_3_out, Q3_q);
  not not_4 (not_4_out, Q0_q);
  not not_5 (not_5_out, Q3_q);
  and and_1 (and_1_out, Q2_q, not_1_out, not_2_out);
  and and_2 (and_2_out, Q3_q, Q1_q);
  and and_3 (and_3_out, Q3_q, Q2_q);
  and and_4 (and_4_out, not_3_out, Q1_q, not_4_out);
  and and_5 (and_5_out, not_5_out, Q2_q);
  and and_6 (and_6_out, Q2_q, Q1_q);
  and and_7 (and_7_out, Q3_q, Q1_q, Q0_q, pronto);
  not not_6 (not_6_out, Q3_q);
  not not_7 (not_7_out, Q2_q);
  not not_8 (not_8_out, Q2_q);
  not not_9 (not_9_out, Q0_q);
  not not_10 (not_10_out, Q0_q);
  not not_11 (not_11_out, Q2_q);
  not not_12 (not_12_out, Q1_q);
  not not_13 (not_13_out, Q0_q);
  not not_14 (not_14_out, Q2_q);
  not not_15 (not_15_out, Q1_q);
  not not_16 (not_16_out, pronto);
  not not_17 (not_17_out, Q2_q);
  or or_1 (or_1_out, and_1_out, and_2_out, and_3_out);
  or or_2 (or_2_out, and_4_out, and_5_out, and_6_out, and_7_out);
  and and_8 (and_8_out, not_6_out, not_7_out, Q0_q, k___textSize);
  and and_9 (and_9_out, not_8_out, Q1_q);
  and and_10 (and_10_out, Q1_q, not_9_out);
  and and_11 (and_11_out, Q3_q, not_10_out);
  and and_12 (and_12_out, not_11_out, not_12_out, not_13_out, data_ok);
  and and_13 (and_13_out, not_14_out, not_15_out, Q0_q, k___textSize);
  and and_14 (and_14_out, Q1_q, Q0_q, not_16_out);
  and and_15 (and_15_out, Q2_q, Q1_q, pronto);
  and and_16 (and_16_out, Q3_q, not_17_out);
  and and_17 (and_17_out, Q3_q, Q0_q);
  or or_3 (or_3_out, and_8_out, and_9_out, and_10_out, and_11_out);
  or or_4 (or_4_out, and_12_out, and_13_out, and_14_out, and_15_out, and_16_out, and_17_out);
  D_Flip_Flop Q3 (.clk(clk), .D(or_1_out), .Q(Q3_q), .reset(rst));  // open: Qn, preset, en
  D_Flip_Flop Q2 (.clk(clk), .D(or_2_out), .Q(Q2_q), .reset(rst));  // open: Qn, preset, en
  D_Flip_Flop Q1 (.clk(clk), .D(or_3_out), .Q(Q1_q), .reset(rst));  // open: Qn, preset, en
  D_Flip_Flop Q0 (.clk(clk), .D(or_4_out), .Q(Q0_q), .reset(rst));  // open: Qn, preset, en
  nor nor_1 (nor_1_out, Q3_q, Q2_q, Q1_q, Q0_q);
  not not_18 (not_18_out, Q3_q);
  not not_19 (not_19_out, Q2_q);
  not not_20 (not_20_out, k___textSize);
  not not_21 (not_21_out, Q1_q);
  not not_22 (not_22_out, Q3_q);
  not not_23 (not_23_out, Q2_q);
  not not_24 (not_24_out, Q1_q);
  not not_25 (not_25_out, Q2_q);
  not not_26 (not_26_out, Q3_q);
  not not_27 (not_27_out, Q0_q);
  not not_28 (not_28_out, Q3_q);
  not not_29 (not_29_out, Q0_q);
  not not_30 (not_30_out, Q1_q);
  not not_31 (not_31_out, Q2_q);
  not not_32 (not_32_out, Q0_q);
  not not_33 (not_33_out, Q0_q);
  not not_34 (not_34_out, Q2_q);
  not not_35 (not_35_out, Q1_q);
  not not_36 (not_36_out, Q0_q);
  not not_37 (not_37_out, Q2_q);
  not not_38 (not_38_out, Q3_q);
  not not_39 (not_39_out, Q1_q);
  not not_40 (not_40_out, Q1_q);
  not not_41 (not_41_out, Q0_q);
  and and_18 (Done, not_18_out, not_19_out, not_20_out, not_21_out, Q0_q);
  not not_42 (not_42_out, Q2_q);
  not not_43 (not_43_out, Q1_q);
  not not_44 (not_44_out, Q0_q);
  not not_45 (not_45_out, Q3_q);
  not not_46 (not_46_out, Q2_q);
  and and_19 (and_19_out, not_22_out, Q2_q, Q1_q, Q0_q);
  and and_20 (and_20_out, Q3_q, not_23_out, Q1_q, Q0_q);
  not not_47 (not_47_out, Q2_q);
  not not_48 (not_48_out, Q0_q);
  not not_49 (not_49_out, Q1_q);
  not not_50 (not_50_out, Q0_q);
  and and_21 (and_21_out, not_25_out, Q1_q, Q0_q);
  and and_22 (and_22_out, not_26_out, Q2_q, not_27_out);
  and and_23 (and_23_out, not_28_out, Q2_q, Q1_q);
  and and_24 (and_24_out, Q2_q, Q1_q, not_29_out);
  and and_25 (and_25_out, Q3_q, Q2_q, not_30_out, Q0_q);
  not not_51 (not_51_out, Q2_q);
  not not_52 (not_52_out, Q0_q);
  not not_53 (not_53_out, Q1_q);
  not not_54 (not_54_out, Q2_q);
  not not_55 (not_55_out, Q0_q);
  not not_56 (not_56_out, Q3_q);
  not not_57 (not_57_out, Q1_q);
  and and_26 (and_26_out, not_31_out, Q1_q, Q0_q);
  and and_27 (and_27_out, Q2_q, Q1_q, not_32_out);
  and and_28 (and_28_out, Q2_q, Q1_q, not_33_out);
  and and_29 (and_29_out, Q3_q, not_34_out, not_35_out);
  not not_58 (not_58_out, Q2_q);
  and and_30 (and_30_out, Q2_q, Q1_q, not_36_out);
  and and_31 (and_31_out, Q3_q, not_37_out, Q1_q, Q0_q);
  and and_32 (and_32_out, not_38_out, Q2_q, not_39_out, Q0_q);
  and and_33 (and_33_out, Q3_q, not_40_out, not_41_out);
  and and_34 (and_34_out, Q3_q, Q2_q, Q1_q);
  and and_35 (indice[1], Q3_q, Q2_q, Q0_q);
  and and_36 (en_k, Q3_q, not_42_out, not_43_out);
  and and_37 (en_j, Q2_q, Q1_q, not_44_out);
  and and_38 (en_i, not_45_out, not_46_out, Q1_q, Q0_q);
  or or_5 (en_t, and_19_out, and_20_out);
  and and_39 (vetor, Q3_q, Q2_q, not_24_out, Q0_q);
  and and_40 (and_40_out, not_47_out, Q1_q, Q0_q);
  and and_41 (and_41_out, Q2_q, Q1_q, not_48_out);
  and and_42 (and_42_out, Q3_q, not_49_out, not_50_out);
  or or_6 (Dado[1], and_21_out, and_22_out, and_23_out, and_24_out, and_25_out);
  and and_43 (and_43_out, not_51_out, Q1_q, not_52_out);
  and and_44 (and_44_out, Q2_q, not_53_out);
  and and_45 (and_45_out, Q3_q, Q2_q);
  and and_46 (and_46_out, not_54_out, Q1_q, not_55_out);
  and and_47 (and_47_out, not_56_out, Q2_q, not_57_out, Q0_q);
  and and_48 (and_48_out, Q3_q, Q2_q, Q1_q);
  or or_7 (out_15, and_26_out, and_27_out);
  or or_8 (B_plus[0], and_28_out, and_29_out);
  and and_49 (B_plus[1], Q3_q, not_58_out, Q0_q);
  or or_9 (A_plus, and_30_out, and_31_out);
  or or_10 (indice[0], and_32_out, and_33_out, and_34_out);
  or or_11 (Dado[0], and_40_out, and_41_out, and_42_out);
  or or_12 (sel, and_43_out, and_44_out, and_45_out);
  or or_13 (ld, and_46_out, and_47_out, and_48_out);
  or or_14 (rst_bd, nor_1_out, rst);
endmodule

module f (
  input  [7:0] rst,
  input  [7:0] A,
  input  [7:0] B,
  input  in_4,
  output pronto
);

  wire clock_1_out, d_ff_1_q, subtractor_1_bout;
  wire [7:0] multiplexer_1_out, multiplexer_2_out, register_1_q, subtractor_1_out;

  Multiplexer #(.width(8)) multiplexer_1 (
    .in0(multiplexer_2_out), .in1(A), .out(multiplexer_1_out), .sel(subtractor_1_bout));  // open: en
  Clock clock_1 (.out(clock_1_out));
  Register register_1 (.D(multiplexer_1_out), .en(in_4), .Q(register_1_q), .clk(clock_1_out));  // open: clr
  Multiplexer #(.width(8)) multiplexer_2 (
    .in0(subtractor_1_out), .in1(register_1_q), .out(multiplexer_2_out), .sel(subtractor_1_bout));  // open: en
  Subtractor subtractor_1 (.a(register_1_q), .b(B), .out(subtractor_1_out), .bout(subtractor_1_bout));  // open: bin
  Register av_atual (.D(multiplexer_2_out), .clk(clock_1_out));  // open: en, Q, clr
  D_Flip_Flop d_ff_1 (.clk(clock_1_out), .D(in_4), .Q(d_ff_1_q));  // open: Qn, preset, en, reset
  and and_1 (pronto, subtractor_1_bout, d_ff_1_q);
endmodule
